# Fritzing sketch 4LED (saved by Fritzing 0.8.3b)
breadboards: 1

parts:
  Part1 = Arduino Uno (Rev3)
  LED1 = LED - 5mm [color="Yellow (585nm)" package="5 mm [THT]"]  # not connected
  LED2 = LED - 5mm [color="Yellow (585nm)" package="5 mm [THT]"]
  LED3 = LED - 5mm [color="Red (633nm)" package="5 mm [THT]"]
  LED4 = LED - 5mm [color="Red (633nm)" package="5 mm [THT]"]
  R1 = Resistor [tolerance=±5% resistance=330 package=THT]
  R2 = Resistor [tolerance=±5% resistance=330 package=THT]
  R3 = Resistor [tolerance=±5% resistance=330 package=THT]
  R4 = Resistor [tolerance=±5% resistance=330 package=THT]

nets:
  N1: Part1.GND, R1.Pin_1, R2.Pin_1, R3.Pin_0, R4.Pin_0
  N2: Part1.D9_PWM, LED4.cathode
  N3: Part1.D10_PWM/SS, LED2.cathode
  N4: Part1.D6_PWM, LED3.cathode
  N5: LED2.anode, R4.Pin_1
  N6: LED3.anode, R2.Pin_0
  N7: LED4.anode, R3.Pin_1
