# Fritzing sketch 4LED_IR (saved by Fritzing 0.8.3b)
breadboards: 1

parts:
  Part1 = Arduino Uno (Rev3)
  LED1 = LED - 5mm [color="Yellow (585nm)" package="5 mm [THT]"]  # not connected
  LED2 = LED - 5mm [color="Yellow (585nm)" package="5 mm [THT]"]
  LED3 = LED - 5mm [color="Red (633nm)" package="5 mm [THT]"]
  LED4 = LED - 5mm [color="Red (633nm)" package="5 mm [THT]"]
  R1 = Resistor [tolerance=±5% resistance=330 package=THT]
  R2 = Resistor [tolerance=±5% resistance=330 package=THT]
  R3 = Resistor [tolerance=±5% resistance=330 package=THT]
  R4 = Resistor [tolerance=±5% resistance=330 package=THT]
  IR1 = TSOP312.., 314.. [package=THT]

nets:
  N1: Part1.GND, R1.Pin_1, R2.Pin_1, R3.Pin_0, R4.Pin_0, IR1.Vs
  N2: Part1.D9_PWM, LED4.cathode
  N3: Part1.D10_PWM/SS, LED2.cathode
  N4: Part1.D3_PWM, IR1.GND
  N5: Part1.D6_PWM, LED3.cathode
  N6: Part1.3V3, IR1.Data
  N7: LED2.anode, R4.Pin_1
  N8: LED3.anode, R2.Pin_0
  N9: LED4.anode, R3.Pin_1
